# Fritzing sketch esp32_xh711 (saved by Fritzing 0.9.3b)

parts:
  U1 = ESP32-38PinWide [part_number=ESP32-38PinWide]
  Componente1 = HX711 Weighing Sensor Module

nets:
  N1: U1.3.3, Componente1.VCC
  GND: U1.GND, Componente1.GND
  N2: U1.GPIO2, Componente1.DO/RX
  N3: U1.GPIO0, Componente1.CK/TX

custom parts:
  ESP32-38PinWide: Generic 38-Pin ESP32 with wide format (only access to one side of pins on a breadboard) based on Stephen Lilley's HiLetgo ESP-WROOM-32 ESP32 ESP-32S Development Board.
