# Fritzing sketch esp32_dht22 (saved by Fritzing 0.9.3b)

parts:
  U1 = ESP32-38PinWide [part_number=ESP32-38PinWide]
  Componente1 = DHT22 module

nets:
  N1: U1.3.3, Componente1.DATA
  GND: U1.GND, Componente1.GND
  N2: U1.GPIO4, Componente1.VCC

custom parts:
  ESP32-38PinWide: Generic 38-Pin ESP32 with wide format (only access to one side of pins on a breadboard) based on Stephen Lilley's HiLetgo ESP-WROOM-32 ESP32 ESP-32S Development Board.
