# Fritzing sketch loadcell_hx711 (saved by Fritzing 0.9.3b)

parts:
  S1 = Load Sensor - 50kg [part_number=SEN-10245]
  S2 = Load Sensor - 50kg [part_number=SEN-10245]
  S3 = Load Sensor - 50kg [part_number=SEN-10245]
  S4 = Load Sensor - 50kg [part_number=SEN-10245]
  hx711 = HX711 Weighing Sensor Module

nets:
  N1: S1.B, S3.B
  N2: S1.W, S2.W
  N3: S1.R, hx711.A+
  N4: S2.B, S4.B
  N5: S2.R, hx711.E+
  N6: S3.W, S4.W
  N7: S3.R, hx711.E-
  N8: S4.R, hx711.A-

custom parts:
  Load Sensor - 50kg: Half-wheatstone bridge Load Cell modified from the Fritzing Repo This load sensor, sometimes called a strain gauge, is the same one found in digital bathroom scales (you know, the ones you use in January for your New Year's resolutions, and then forget about a month later). This sensor can measure up to about 110 pounds.
